# Fritzing sketch WiFiThermometer (saved by Fritzing 0.9.3b)
breadboards: 1

parts:
  Part1 = Arduino Uno (Rev3)
  T1 = LM35 Temperature Sensor [package="TO92 [THT]"]
  U1 = ESP8266 WiFi Module [part_number=ESP8266]

nets:
  N1: Part1.A1, T1.Vout
  GND: Part1.GND, T1.GND, U1.GND
  N2: Part1.D2, U1.TXD
  N3: Part1.D3_PWM, U1.RXD
  3V3: Part1.3V3, U1.VCC, U1.CH_PD
  N4: Part1.5V, T1.+Vs

custom parts:
  ESP8266 WiFi Module: Generic WiFi Module based on the ESP8266 with onboard PCB antenna and UART communications
